// Logisim project Project.All.circ as structural Verilog: 4 circuits, main circuit main
module main (
  input  in_1,
  input  in_2,
  input  in_3,
  input  in_4,
  input  in_5,
  input  in_6,
  input  in_7,
  input  in_8,
  input  in_9,
  input  in_10,
  input  in_11,
  input  in_12,
  input  in_13,
  input  in_14,
  input  in_15,
  input  in_16,
  input  in_17,
  input  in_18,
  input  in_19,
  input  in_20,
  input  in_21,
  output out_22,
  output out_23,
  output out_24,
  output out_25,
  output out_26,
  output out_27
);

  wire adder_1_a_2, adder_1_b_2, adder_2_a_2, adder_2_b_2, adder_3_a_2, adder_3_b_2, mux_1_out_7,
       mux_2_out_7, mux_3_out_7, mux_4_out_7, segement_1_a, segement_1_b_2, segement_1_c_2, segement_1_d_2,
       segement_1_e, segement_1_f, segement_1_g, xor_1_out, xor_2_out, xor_3_out, xor_4_out;

  and and_1 (out_22, in_7, in_8);
  and and_2 (out_23, in_9, in_10);
  and and_3 (out_24, in_12, in_13);
  or or_1 (out_22, in_16, in_17);
  or or_2 (out_26, in_18, in_19);
  or or_3 (out_27, in_20, in_21);
  xor xor_1 (xor_1_out, in_4, in_14);
  xor xor_2 (xor_2_out, in_5, in_14);
  xor xor_3 (xor_3_out, in_6, in_14);
  Adder adder_1 (.a(in_1), .b(xor_1_out), .c(in_14), .A_2(adder_1_a_2), .B_2(adder_1_b_2));
  Adder adder_2 (.a(in_2), .b(xor_2_out), .c(adder_1_b_2), .A_2(adder_2_a_2), .B_2(adder_2_b_2));
  Adder adder_3 (.a(in_3), .b(xor_3_out), .c(adder_2_b_2), .A_2(adder_3_a_2), .B_2(adder_3_b_2));
  xor xor_4 (xor_4_out, adder_3_b_2, in_14);
  Mux mux_1 (
    .in_1(adder_1_a_2), .in_2(out_24), .in_3(out_27), .in_4(adder_1_a_2), .in_5(in_14), .in_6(in_15),
    .out_7(mux_1_out_7));
  Mux mux_2 (
    .in_1(adder_2_a_2), .in_2(out_23), .in_3(out_26), .in_4(adder_2_a_2), .in_5(in_14), .in_6(in_15),
    .out_7(mux_2_out_7));
  Mux mux_3 (
    .in_1(adder_3_a_2), .in_2(out_22), .in_3(out_22), .in_4(adder_3_a_2), .in_5(in_14), .in_6(in_15),
    .out_7(mux_3_out_7));
  Mux mux_4 (
    .in_1(xor_4_out), .in_2(in_11), .in_3(in_11), .in_4(xor_4_out), .in_5(in_14), .in_6(in_15),
    .out_7(mux_4_out_7));
  Segement segement_1 (
    .in_1(mux_4_out_7), .b(mux_3_out_7), .c(mux_2_out_7), .d(mux_1_out_7), .A(segement_1_a),
    .B_2(segement_1_b_2), .C_2(segement_1_c_2), .D_2(segement_1_d_2), .E(segement_1_e), .F(segement_1_f),
    .G(segement_1_g));
  _7_Segment_Display u_7_segment_display_1 (
    .g(segement_1_a), .f(segement_1_b_2), .a(segement_1_c_2), .b(segement_1_d_2), .e(segement_1_g),
    .d(segement_1_f), .c(segement_1_e));  // open: dp

  assign out_25 = out_22;
endmodule

module Adder (
  input  a,
  input  b,
  input  c,
  output A_2,
  output B_2
);

  wire and_1_out, and_2_out, and_3_out, and_4_out, and_5_out, and_6_out, and_7_out, not_1_out, not_2_out,
       not_3_out, not_4_out, not_5_out, not_6_out;

  not not_1 (not_1_out, a);
  not not_2 (not_2_out, b);
  not not_3 (not_3_out, a);
  not not_4 (not_4_out, c);
  not not_5 (not_5_out, b);
  not not_6 (not_6_out, c);
  and and_1 (and_1_out, not_1_out, not_2_out, c);
  and and_2 (and_2_out, not_3_out, b, not_4_out);
  and and_3 (and_3_out, a, not_5_out, not_6_out);
  and and_4 (and_4_out, a, b, c);
  and and_5 (and_5_out, a, b);
  and and_6 (and_6_out, b, c);
  or or_1 (B_2, and_5_out, and_6_out, and_7_out);
  and and_7 (and_7_out, a, c);
  or or_2 (A_2, and_1_out, and_2_out, and_3_out, and_4_out);
endmodule

module Segement (
  input  in_1,
  input  b,
  input  c,
  input  d,
  output A,
  output B_2,
  output C_2,
  output D_2,
  output E,
  output F,
  output G
);

  wire and_1_out, and_2_out, and_3_out, and_4_out, and_5_out, and_6_out, and_7_out, and_8_out, and_9_out,
       and_10_out, and_11_out, and_12_out, and_13_out, and_14_out, and_15_out, and_16_out, not_1_out,
       not_2_out, not_3_out, not_4_out, not_5_out, not_6_out, not_7_out, not_8_out, not_9_out, not_10_out,
       not_11_out, not_12_out, not_13_out, not_14_out, not_15_out, not_16_out, not_17_out, not_18_out,
       not_19_out, not_20_out, not_21_out;

  not not_1 (not_1_out, b);
  and and_1 (and_1_out, not_1_out, c);
  and and_2 (and_2_out, b, not_2_out);
  not not_2 (not_2_out, c);
  and and_3 (and_3_out, b, not_3_out);
  not not_3 (not_3_out, d);
  not not_4 (not_4_out, c);
  and and_4 (and_4_out, not_4_out, not_5_out);
  not not_5 (not_5_out, d);
  and and_5 (and_5_out, b, not_6_out);
  not not_6 (not_6_out, c);
  and and_6 (and_6_out, b, not_7_out);
  not not_7 (not_7_out, d);
  not not_8 (not_8_out, b);
  and and_7 (and_7_out, not_8_out, not_9_out);
  not not_9 (not_9_out, d);
  and and_8 (and_8_out, b, d);
  not not_10 (not_10_out, b);
  not not_11 (not_11_out, c);
  and and_9 (and_9_out, not_11_out, not_12_out);
  not not_12 (not_12_out, d);
  and and_10 (and_10_out, c, d);
  not not_13 (not_13_out, c);
  or or_1 (E, not_13_out, d, b);
  not not_14 (not_14_out, b);
  and and_11 (and_11_out, not_14_out, not_15_out);
  not not_15 (not_15_out, d);
  not not_16 (not_16_out, b);
  and and_12 (and_12_out, not_16_out, c);
  and and_13 (and_13_out, c, not_17_out);
  not not_17 (not_17_out, d);
  not not_18 (not_18_out, c);
  and and_14 (and_14_out, b, not_18_out, d);
  not not_19 (not_19_out, b);
  and and_15 (and_15_out, not_19_out, not_20_out);
  not not_20 (not_20_out, d);
  and and_16 (and_16_out, c, not_21_out);
  not not_21 (not_21_out, d);
  or or_2 (A, and_1_out, and_2_out, and_3_out, in_1);
  or or_3 (B_2, and_4_out, and_5_out, and_6_out, in_1);
  or or_4 (C_2, and_7_out, c, and_8_out, in_1);
  or or_5 (D_2, not_10_out, and_9_out, and_10_out);
  or or_6 (F, and_11_out, and_12_out, and_13_out, and_14_out, in_1);
  or or_7 (G, and_15_out, and_16_out);
endmodule

module Mux (
  input  in_1,
  input  in_2,
  input  in_3,
  input  in_4,
  input  in_5,
  input  in_6,
  output out_7
);

  wire and_1_out, and_2_out, and_3_out, and_4_out, not_1_out, not_2_out;

  not not_1 (not_1_out, in_5);
  not not_2 (not_2_out, in_6);
  and and_1 (and_1_out, in_1, not_1_out, not_2_out);
  and and_2 (and_2_out, in_2, not_1_out, in_6);
  and and_3 (and_3_out, in_3, in_5, not_2_out);
  and and_4 (and_4_out, in_4, in_5, in_6);
  or or_1 (out_7, and_1_out, and_2_out, and_3_out, and_4_out);
endmodule
